# Fritzing sketch TSFRL_master_module (saved by Fritzing 0.9.0b)
circuit board: 6.08472cm x 5.3848cm
circuit board: 9cm x 7cm
perfboards: 1

parts:
  Data = LED - 3mm [color="Yellow (595nm)" package="3 mm [THT]"]
  keyStart = Pushbutton [package="[THT]"]
  keyRight = Pushbutton [package="[THT]"]
  keyReset = Pushbutton [package="[THT]"]
  11_male_pins = male pin header, 11 pins [form="♂ (male)"]
  Error = LED - 3mm [color="Red (660nm)" package="3 mm [THT]"]
  Done = LED - 3mm [color="Green (570nm)" package="3 mm [THT]"]
  keyLeft = Pushbutton [package="[THT]"]
  keyDown = Pushbutton [package="[THT]"]
  Start = LED - 3mm [color="Blue (525nm)" package="3 mm [THT]"]
  keyUp = Pushbutton [package="[THT]"]
  C = Hex Inverter Schmitt Trigger SN74HC14 [package="DIP (Dual Inline)"]
  11_male_pins1 = male pin header, 11 pins [form="♂ (male)"]
  keySTOP/CANCEL = Pushbutton [package="[THT]"]
  keyDOWN = Pushbutton [package="[THT]"]
  keyLEFT = Pushbutton [package="[THT]"]
  keyUP = Pushbutton [package="[THT]"]
  R1 = Resistor [tolerance=±5% resistance=10k package=THT]
  R3 = Resistor [tolerance=±5% resistance=10k package=THT]
  R4 = Resistor [tolerance=±5% resistance=100k package=THT]
  C2 = Ceramic Capacitor [capacitance=100nF package="100 mil [THT, multilayer]"]
  R2 = Resistor [tolerance=±5% resistance=100k package=THT]
  R7 = Resistor [tolerance=±5% resistance=10k package=THT]
  R8 = Resistor [tolerance=±5% resistance=100k package=THT]
  C4 = Ceramic Capacitor [capacitance=100nF package="100 mil [THT, multilayer]"]
  C1 = Ceramic Capacitor [capacitance=100nF package="100 mil [THT, multilayer]"]
  keyRIGHT1 = Pushbutton [package="[THT]"]
  C6 = Ceramic Capacitor [capacitance=100nF package="100 mil [THT, multilayer]"]
  keySTART1 = Pushbutton [package="[THT]"]
  C7 = Ceramic Capacitor [capacitance=100nF package="100 mil [THT, multilayer]"]
  R12 = Resistor [tolerance=±5% resistance=100k package=THT]
  R11 = Resistor [tolerance=±5% resistance=10k package=THT]
  R14 = Resistor [tolerance=±5% resistance=100k package=THT]
  R13 = Resistor [tolerance=±5% resistance=10k package=THT]

nets (from the schematic view):
  GND: Data.cathode, keyStart.Pin_1, keyStart.Pin_2, keyRight.Pin_1, keyRight.Pin_2, keyReset.Pin_1, keyReset.Pin_2, 11_male_pins.pin1, Error.cathode, Done.cathode, keyLeft.Pin_1, keyLeft.Pin_2, keyDown.Pin_1, keyDown.Pin_2, keyUp.Pin_1, keyUp.Pin_2, C.GND, 11_male_pins1.pin1, keySTOP/CANCEL.Pin_3, keyDOWN.Pin_3, keyLEFT.Pin_3, keyUP.Pin_3, C2.0, C4.0, C1.0, keyRIGHT1.Pin_3, C6.0, keySTART1.Pin_3, C7.0
  N1: Data.anode, 11_male_pins.pin8
  N2: keyStart.Pin_3, keyStart.Pin_4, 11_male_pins.pin4
  N3: keyRight.Pin_3, keyRight.Pin_4, 11_male_pins.pin6
  N4: keyReset.Pin_3, keyReset.Pin_4, 11_male_pins.pin2
  N5: 11_male_pins.pin3, keyDown.Pin_3, keyDown.Pin_4
  N6: 11_male_pins.pin5, keyLeft.Pin_3, keyLeft.Pin_4
  N7: 11_male_pins.pin7, keyUp.Pin_3, keyUp.Pin_4
  N8: 11_male_pins.pin9, Error.anode
  N9: 11_male_pins.pin10, Done.anode
  N10: 11_male_pins.pin11, Start.anode
  N11: C.1A, R2.Pin_1, C1.1
  keyUP_out: C.1Y
  N12: C.2A, R4.Pin_1, C2.1
  keyLEFT_out: C.2Y
  N13: C.4A, C6.1, R12.Pin_1
  keyDOWN_out: C.5Y
  N14: C.5A, R8.Pin_1, C4.1
  N15: C.6A, C7.1, R14.Pin_1
  5V: C.VCC, 11_male_pins1.pin2, R1.Pin_1, R3.Pin_1, R7.Pin_1, R11.Pin_1, R13.Pin_1
  N16: keyDOWN.Pin_1, keyDOWN.Pin_2, R7.Pin_0, R8.Pin_0
  N17: keyLEFT.Pin_1, keyLEFT.Pin_2, R3.Pin_0, R4.Pin_0
  N18: keyUP.Pin_1, keyUP.Pin_2, R1.Pin_0, R2.Pin_0
  N19: keyRIGHT1.Pin_1, keyRIGHT1.Pin_2, R12.Pin_0, R11.Pin_0
  N20: keySTART1.Pin_1, keySTART1.Pin_2, R14.Pin_0, R13.Pin_0
