# Fritzing sketch TSFRL_power_module_and_data_bus (saved by Fritzing 0.9.0b)

parts:
  IC1 = Voltage Regulator [package=to220-igo]
  C1 = Capacitor Polarized [package=cpol-radial-100uf-25v]
  R1 = Resistor [tolerance=±5% resistance=220 package=THT]
  POWER = LED - 3mm [color="Red (633nm)" package="3 mm [THT]"]
  DATA_pins = male pin header, 5 pins [form="♂ (male)"]
  C2 = Capacitor Polarized [package=cpol-radial-10uf-16v]

nets:
  GND: IC1.GND, C1.-, POWER.cathode, DATA_pins.pin2, C2.-
  12V: IC1.IN, C1.+
  N1: IC1.OUT, R1.Pin_0, C2.+
  5V: R1.Pin_1, POWER.anode, DATA_pins.pin1

notes:
  TSFRL_master_module_keys
  8) +5v
  7) keyUP
  6) keyRIGHT
  5) keyLEFT
  4) keyDOWN
  3)keySTART
  2)keySTOP/CANCEL
  1)GND
  GND
  VCC +5V
  CANCEL signal
  RS485_a
  RS485_b
  Test Stand For Radio Lamps, Test Stand For Radio Lamps project: power module and data bus, 1.0

custom parts:
  Capacitor Polarized: Capacitor Polarized cpol-radial-10uf-16v
