# Fritzing sketch TSFRL_slave_module (saved by Fritzing 0.9.0b)
circuit board: 9cm x 7cm
perfboards: 1

parts:
  DATA/POWER_pins = male pin header, 5 pins [form="♂ (male)"]
  DATA = LED - 3mm [color="Yellow (595nm)" package="3 mm [THT]"]
  ARDUINO_NANO = Arduino Nano (Rev3.0)
  R1 = Resistor [tolerance=±5% resistance=220 package=THT]
  U2 = DS75176BN [package=dil08]
  Q1 = NPN-Transistor [part_number=BC547B package="TO92 [THT]"]
  R2 = Resistor [tolerance=±5% resistance=0 part_number=8,6k package=THT]
  Q3 = NPN-Transistor [part_number=BC547B package="TO92 [THT]"]
  Q4 = NPN-Transistor [part_number=BC547B package="TO92 [THT]"]
  Q5 = NPN-Transistor [part_number=BC547B package="TO92 [THT]"]
  Q2 = NPN-Transistor [part_number=BC547B package="TO92 [THT]"]
  J1 = male pin header, 4 pins [form="♂ (male)"]
  R3 = Resistor [tolerance=±5% resistance=0 part_number=8,6k package=THT]
  R4 = Resistor [tolerance=±5% resistance=0 part_number=8,6k package=THT]
  R6 = Resistor [tolerance=±5% resistance=0 part_number=8,6k package=THT]
  R7 = Resistor [tolerance=±5% resistance=220 package=THT]
  LED1 = LED - 3mm [color="White (4500K)" package="3 mm [THT]"]
  R8 = Resistor [tolerance=±5% resistance=220 package=THT]
  LED2 = LED - 3mm [color="White (4500K)" package="3 mm [THT]"]
  R9 = Resistor [tolerance=±5% resistance=220 package=THT]
  LED3 = LED - 3mm [color="White (4500K)" package="3 mm [THT]"]
  R10 = Resistor [tolerance=±5% resistance=220 package=THT]
  LED4 = LED - 3mm [color="White (4500K)" package="3 mm [THT]"]
  R5 = Resistor [tolerance=±5% resistance=0 part_number=8,6k package=THT]

nets:
  GND: DATA/POWER_pins.pin1, DATA.cathode, ARDUINO_NANO.GND, U2.GND, LED1.cathode, LED2.cathode, LED3.cathode, LED4.cathode
  N1: DATA/POWER_pins.pin2, U2.DO/RI#5
  N2: DATA/POWER_pins.pin3, U2.DO/RI#6
  5V: DATA/POWER_pins.pin4, ARDUINO_NANO.5V, U2.VCC
  N3: DATA/POWER_pins.pin5, ARDUINO_NANO.RESET
  N4: DATA.anode, R1.Pin_1
  N5: ARDUINO_NANO.D2, R7.Pin_0
  N6: ARDUINO_NANO.D3, R8.Pin_0
  N7: ARDUINO_NANO.D4, R9.Pin_0
  N8: ARDUINO_NANO.D5, R10.Pin_0
  N9: ARDUINO_NANO.D6, R2.Pin_0
  N10: ARDUINO_NANO.D7, R3.Pin_0
  N11: ARDUINO_NANO.D8, R4.Pin_0
  N12: ARDUINO_NANO.D9, R5.Pin_0
  N13: ARDUINO_NANO.D10, R6.Pin_0
  N14: ARDUINO_NANO.D11/MOSI, U2.DI
  N15: ARDUINO_NANO.D12/MISO, U2.RO
  N16: ARDUINO_NANO.A4, J1.pin4
  N17: ARDUINO_NANO.A3, J1.pin3
  N18: ARDUINO_NANO.A2, J1.pin2
  N19: ARDUINO_NANO.A1, J1.pin1
  N20: ARDUINO_NANO.D13/SCK, R1.Pin_0, U2.RE, U2.DE
  To Lamp_section: Q1.E, Q3.E, Q4.E, Q5.E, Q2.E
  N21: Q1.B, R2.Pin_1
  Voltage_1: Q1.C
  N22: Q3.B, R4.Pin_1
  Voltage_3: Q3.C
  N23: Q4.B, R5.Pin_1
  Voltage_4: Q4.C
  N24: Q5.B, R6.Pin_1
  Voltage_5: Q5.C
  N25: Q2.B, R3.Pin_1
  Voltage_2: Q2.C
  N26: R7.Pin_1, LED1.anode
  N27: R8.Pin_1, LED2.anode
  N28: R9.Pin_1, LED3.anode
  N29: R10.Pin_1, LED4.anode

notes:
  GND
  VCC +5V
  RESET signal
  RS485_a
  RS485_b
  Test Stand For Radio Lamps, Test Stand For Radio Lamps project: slave module, 1.0
  DATA/POWER_pins
  1) RESET signal
  2) +5v
  3) RS485_a
  4) RS485_b
  5) GND

custom parts:
  DS75176BN: RS-485 transceiver
